# Fritzing sketch formation (saved by Fritzing 0.8.7b)
breadboards: 1

parts:
  Composant1 = Arduino Uno (Rev3)
  DHT1 = Humidity and Temperature Sensor DHT11
  LED1 = LED - 5mm [color="Yellow (595nm)" package="5 mm [THT]"]
  LED2 = LED - 5mm [color="Red (633nm)" package="5 mm [THT]"]
  LED3 = LED - 5mm [color="Green (570nm)" package="5 mm [THT]"]
  R1 = Resistor [tolerance=±5% resistance=220 package=THT]
  R2 = Resistor [tolerance=±5% resistance=220 package=THT]
  R3 = Resistor [tolerance=±5% resistance=220 package=THT]

nets:
  N1: Composant1.A0, DHT1.Data-signal
  N2: Composant1.D11_PWM/MOSI, R2.Pin_1
  N3: Composant1.D12/MISO, R3.Pin_1
  5V: Composant1.5V, DHT1.Vcc
  N4: Composant1.GND, DHT1.GND_2, LED1.cathode, LED2.cathode, LED3.cathode
  N5: LED1.anode, R2.Pin_0
  N6: LED2.anode, R3.Pin_0
  N7: LED3.anode, R1.Pin_0

custom parts:
  Humidity and Temperature Sensor DHT11: Digital relative humidity & temperature sensor DHT11
